// Logisim project 3_Bit_Full_Adder.circ as structural Verilog: 1 circuit, main circuit main
module main (
  input  CIN,
  input  A1,
  input  B1,
  input  A2,
  input  B2,
  input  A3,
  input  B3,
  output OUT1,
  output OUT2,
  output OUT3,
  output COUT
);

  wire and_1_out, and_2_out, and_3_out, and_4_out, and_5_out, and_6_out, or_1_out, or_2_out, xor_1_out,
       xor_2_out, xor_3_out;

  xor xor_1 (xor_1_out, A1, B1);
  and and_1 (and_1_out, A1, B1);
  xor xor_2 (xor_2_out, A2, B2);
  and and_2 (and_2_out, A2, B2);
  xor xor_3 (xor_3_out, A3, B3);
  and and_3 (and_3_out, A3, B3);
  and and_4 (and_4_out, CIN, xor_1_out);
  and and_5 (and_5_out, or_1_out, xor_2_out);
  and and_6 (and_6_out, or_2_out, xor_3_out);
  xor xor_4 (OUT1, CIN, xor_1_out);
  or or_1 (or_1_out, and_4_out, and_1_out);
  xor xor_5 (OUT2, or_1_out, xor_2_out);
  or or_2 (or_2_out, and_5_out, and_2_out);
  xor xor_6 (OUT3, or_2_out, xor_3_out);
  or or_3 (COUT, and_6_out, and_3_out);
endmodule
