// Logisim project 3_Bit_Register.circ as structural Verilog: 1 circuit, main circuit main
module main (
  input  Data_1,
  input  Data_2,
  input  Data_3,
  input  Write,
  input  Read
);

  wire and_1_out, and_2_out, and_3_out, and_4_out, and_5_out, and_6_out, and_7_out, and_9_out, and_11_out,
       not_1_out, not_2_out, not_3_out, not_4_out, not_5_out, not_6_out, or_1_out, or_2_out, or_3_out;

  and and_1 (and_1_out, Data_1, Write);
  not not_1 (not_1_out, Data_1);
  and and_2 (and_2_out, not_1_out, Write);
  and and_3 (and_3_out, Data_2, Write);
  not not_2 (not_2_out, Data_2);
  and and_4 (and_4_out, not_2_out, Write);
  and and_5 (and_5_out, Data_3, Write);
  not not_3 (not_3_out, Data_3);
  and and_6 (and_6_out, not_3_out, Write);
  or or_1 (or_1_out, and_7_out, and_1_out);
  and and_7 (and_7_out, or_1_out, not_4_out);
  not not_4 (not_4_out, and_2_out);
  and and_8 (Data_1, and_7_out, Read);
  or or_2 (or_2_out, and_9_out, and_3_out);
  and and_9 (and_9_out, or_2_out, not_5_out);
  not not_5 (not_5_out, and_4_out);
  and and_10 (Data_2, and_9_out, Read);
  or or_3 (or_3_out, and_11_out, and_5_out);
  and and_11 (and_11_out, or_3_out, not_6_out);
  not not_6 (not_6_out, and_6_out);
  and and_12 (Data_3, and_11_out, Read);
endmodule
